# Fritzing sketch circuit (saved by Fritzing 1.0.4)

parts:
  Parça1 = Arduino Uno (Rev3) - ICSP
  L298N1 = L298N DC motor driver
  Parça2 = Soil Moisture Sensor
  Parça3 = LCD1602-I2C
  WATER_PUMP1 = prefix0000  # not connected
  BAT1 = 18650 battery holder [package=battery-18650-kit]  # not connected

nets:
  N1: Parça1.A0, Parça2.SIG
  N2: Parça1.A4/SDA, Parça3.SDA
  N3: Parça1.A5/SCL, Parça3.SCL
  VCC: Parça1.5V, Parça2.VCC, Parça3.VCC
  N4: Parça1.D9_PWM, L298N1.IN1
  N5: Parça1.D10_PWM/SS, L298N1.IN2
  GND: Parça1.GND, Parça2.GND, Parça3.GND

custom parts:
  L298N DC motor driver: 2x DC motor driver with 78M05 positive voltage regulator (7..35 V) L298N: max 46 V, 2 A Set 5 V Enable jumper to enable 5 V regultor (needed for the L298N) and +5 V output at screw terminal or supply external +5 V at screw terminal Set ENA and/or ENB to +5 V to enable motor permanently or supply ENA and/or ENB with PWM signal IN1 and IN2 set rotation directory for motor A (OUT1/OUT2) IN2 and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
  LCD1602-I2C: A standard character display, usually with 2x16 characters. Comes in many colors with LCM1602 IIC attached.
  18650 battery holder: 18650 Battery Holder
